// Logisim project playground.circ as structural Verilog: 1 circuit, main circuit main
module main (
  input  [31:0] in_1,
  input  [31:0] in_2,
  output [31:0] out_3
);

  wire mips_alu_1_p4, registerfile_1_p2, registerfile_1_p3;
  wire [31:0] registerfile_1_p1;

  // RegisterFile registerfile_1: pin names not known; wires that end beside it: registerfile_1_p1, registerfile_1_p2, registerfile_1_p3, registerfile_1_p3, registerfile_1_p2
  // MIPSProgramROM mipsprogramrom_1: pin names not known; wires that end beside it: registerfile_1_p1
  // PLA pla_1: pin names not known; wires that end beside it: registerfile_1_p1[31:26]
  // MIPS_ALU mips_alu_1: pin names not known; wires that end beside it: in_1, in_2, out_3, mips_alu_1_p4
  LED led_1 (.in(mips_alu_1_p4));
endmodule
