// Logisim project mips_single_cycle_rob.circ as structural Verilog: 2 circuits, main circuit main
module main (
);

  wire and_1_out, clock, control_1_alusrc, control_1_branch, control_1_jump, control_1_memread,
       control_1_memtoreg, control_1_memwrite, control_1_regdst, control_1_regwrite, mips_alu_1_p4,
       registerfile_1_p7;
  wire [3:0] control_1_alu;
  wire [4:0] multiplexer_1_out;
  wire [27:0] bit_extender_1_out, shifter_1_out;
  wire [31:0] adder_1_p3, adder_2_p3, bit_extender_2_out, mips_alu_1_p2, mips_alu_1_p5, mips_ram_1_p5,
       mipsprogramrom_1_p2, multiplexer_3_out, multiplexer_4_out, register_1_q, registerfile_1_p1,
       registerfile_1_p8, shifter_2_out;

  Clock clock_1 (.out(clock));
  Register #(.width(32)) register_1 (.D(multiplexer_4_out), .Q(register_1_q), .clk(clock));  // open: en, clr
  // Adder adder_1: pin names not known; wires that end beside it: register_1_q, 32'h4, adder_1_p3
  // MIPSProgramROM mipsprogramrom_1: pin names not known; wires that end beside it: register_1_q, mipsprogramrom_1_p2
  assign bit_extender_1_out = {{2{1'b0}}, mipsprogramrom_1_p2[25:0]};  // Bit_Extender bit_extender_1
  Shifter #(.width(28)) shifter_1 (.in(bit_extender_1_out), .\dist (5'b00010), .out(shifter_1_out));
  Control control_1 (
    .Funct_0_5(mipsprogramrom_1_p2[5:0]), .Opcode_6_11(mipsprogramrom_1_p2[31:26]), .ALU(control_1_alu),
    .Jump(control_1_jump), .Branch(control_1_branch), .MemWrite(control_1_memwrite),
    .MemRead(control_1_memread), .RegWrite(control_1_regwrite), .MemtoReg(control_1_memtoreg),
    .ALUsrc(control_1_alusrc), .RegDst(control_1_regdst));
  Multiplexer #(.width(5), .enable("false")) multiplexer_1 (
    .in0(mipsprogramrom_1_p2[20:16]), .in1(mipsprogramrom_1_p2[15:11]), .out(multiplexer_1_out),
    .sel(control_1_regdst));
  assign bit_extender_2_out = {{16{1'b0}}, mipsprogramrom_1_p2[15:0]};  // Bit_Extender bit_extender_2
  // RegisterFile registerfile_1: pin names not known; wires that end beside it: registerfile_1_p1, clock, control_1_regwrite, multiplexer_1_out, mipsprogramrom_1_p2[25:21], mipsprogramrom_1_p2[20:16], registerfile_1_p7, registerfile_1_p8
  Shifter #(.width(32)) shifter_2 (.in(bit_extender_2_out), .\dist (5'b00010), .out(shifter_2_out));
  // MIPS_ALU mips_alu_1: pin names not known; wires that end beside it: registerfile_1_p7, mips_alu_1_p2, control_1_alu, mips_alu_1_p4, mips_alu_1_p5
  Multiplexer #(.width(32), .enable("false")) multiplexer_2 (
    .in0(registerfile_1_p8), .in1(bit_extender_2_out), .out(mips_alu_1_p2), .sel(control_1_alusrc));
  // Adder adder_2: pin names not known; wires that end beside it: adder_1_p3, shifter_2_out, adder_2_p3
  Multiplexer #(.width(32), .enable("false")) multiplexer_3 (
    .in0(adder_1_p3), .in1(adder_2_p3), .out(multiplexer_3_out), .sel(and_1_out));
  and and_1 (and_1_out, control_1_branch, mips_alu_1_p4);
  Multiplexer #(.width(32), .enable("false")) multiplexer_4 (
    .in0(multiplexer_3_out), .in1({adder_1_p3[31:28], shifter_1_out}), .out(multiplexer_4_out),
    .sel(control_1_jump));
  // MIPS_RAM mips_ram_1: pin names not known; wires that end beside it: registerfile_1_p8, control_1_memwrite, control_1_memread, clock, mips_ram_1_p5
  Multiplexer #(.width(32), .enable("false")) multiplexer_5 (
    .in0(mips_alu_1_p5), .in1(mips_ram_1_p5), .out(registerfile_1_p1), .sel(control_1_memtoreg));
endmodule

// Main Control
module Control (
  input  [5:0] Funct_0_5,
  input  [5:0] Opcode_6_11,
  output [3:0] ALU,
  output Jump,
  output Branch,
  output MemWrite,
  output MemRead,
  output RegWrite,
  output MemtoReg,
  output ALUsrc,
  output RegDst
);

  // PLA pla_1: pin names not known; wires that end beside it: {Opcode_6_11, Funct_0_5}, {RegDst, ALUsrc, MemtoReg, RegWrite, MemRead, MemWrite, Branch, Jump, ALU}
endmodule
